# Fritzing sketch ArduinoCurrentStageSketch (saved by Fritzing 0.9.3b)
breadboards: 1

parts:
  Part1 = Arduino Mega 2560 (Rev3)
  Part2 = Bluetooth HC-05 Macho
  hc-sr1 = hc-sr04
  hc-sr2 = hc-sr04

nets:
  N1: Part1.D15/RX3, Part2.TXD
  N2: Part1.D14/TX3, Part2.RXD
  GND: Part1.GND, Part2.GND, hc-sr1.GND, hc-sr2.GND
  N3: Part1.D5_PWM, hc-sr2.Echo
  N4: Part1.D6_PWM, hc-sr2.Trig
  VCC: Part1.5V, Part2.VCC, hc-sr1.VCC, hc-sr2.VCC
  N5: Part1.D35, hc-sr1.Trig
  N6: Part1.D37, hc-sr1.Echo
